# Fritzing sketch LearPressure_Sketch (saved by Fritzing 0.9.4)
breadboards: 2

parts:
  U1 = ENCODER-QUADRATURE [package=encoder-16mm-quad]
  PRESSURE_SENS = MPX2010 pressure sensor [part_number=MPX]  # not connected
  Mod1 = generic-ac-power-supply [package=THT]
  Onderdeel3 = Arduino Uno (Rev3)
  LCD3 = LCD screen
  LCM1602_IIC4 = LCM1602 IIC [part_number="LCM1602 IIC" chip_label="LCM1602 IIC" package="DIP (Dual Inline) [THT]"]
  EL817_1 = Sharp PC817 [package=THT]
  TIP120_2 = npn-Powertransistor [package="TO220 [THT]"]
  R3 = Resistor [tolerance=±5% resistance=220 package="0603 [SMD]"]
  R4 = Resistor [tolerance=±5% resistance=1k package="0603 [SMD]"]
  IN = Solenoid
  EL817_2 = Sharp PC817 [package=THT]
  TIP120_3 = npn-Powertransistor [package="TO220 [THT]"]
  R5 = Resistor [tolerance=±5% resistance=220 package="0603 [SMD]"]
  R6 = Resistor [tolerance=±5% resistance=1k package="0603 [SMD]"]
  OUT = Solenoid
  S1 = Pushbutton [package="[SMD]"]
  Mod2 = generic-ac-power-supply [package=THT]
  S2 = Pushbutton [package="[SMD]"]
  S3 = Pushbutton [package="[SMD]"]
  MAIN_SW = SWITCH_SPDT [package=kps-1290]
  D1 = Rectifier Diode [part_number=1N4001 package="Melf DO-213 AB [SMD]"]
  D2 = Rectifier Diode [part_number=1N4001 package="Melf DO-213 AB [SMD]"]

nets:
  N1: U1.A, Onderdeel3.D2
  GND: U1.B, Mod1.pin3#3, Onderdeel3.GND, LCM1602_IIC4.GND, S1.Pin_4, S2.Pin_3, S2.Pin_4, S3.Pin_3, S3.Pin_4
  N2: U1.C, Onderdeel3.D3_PWM
  N3: Mod1.pin1, Mod2.pin2, MAIN_SW.P
  N4: Mod1.pin2, Mod2.pin1
  5V: Mod1.pin3#2, Onderdeel3.5V, LCM1602_IIC4.VCC
  N5: Onderdeel3.A4/SDA, LCM1602_IIC4.SDA
  N6: Onderdeel3.A5/SCL, LCM1602_IIC4.SCL
  N7: Onderdeel3.D8, R5.Pin_0
  N8: Onderdeel3.D4, S1.Pin_2
  N9: Onderdeel3.D5_PWM, S3.Pin_1, S3.Pin_2
  N10: Onderdeel3.D6_PWM, S2.Pin_1, S2.Pin_2
  N11: Onderdeel3.D7, R3.Pin_0
  VSS: LCD3.VSS, LCM1602_IIC4.VSS
  VDD: LCD3.VDD, LCM1602_IIC4.VDD
  N12: LCD3.V0, LCM1602_IIC4.V0
  N13: LCD3.RS, LCM1602_IIC4.RS
  N14: LCD3.R/W, LCM1602_IIC4.RW
  N15: LCD3.E, LCM1602_IIC4.E
  N16: LCD3.DB0, LCM1602_IIC4.D0
  N17: LCD3.DB1, LCM1602_IIC4.D1
  N18: LCD3.DB2, LCM1602_IIC4.D2
  N19: LCD3.DB3, LCM1602_IIC4.D3
  N20: LCD3.DB4, LCM1602_IIC4.D4
  N21: LCD3.DB5, LCM1602_IIC4.D5
  N22: LCD3.DB6, LCM1602_IIC4.D6
  N23: LCD3.DB7, LCM1602_IIC4.D7
  N24: LCD3.LED+, LCM1602_IIC4.A
  N25: LCD3.LED-, LCM1602_IIC4.K
  N26: LCM1602_IIC4.LED_A, LCM1602_IIC4.LED_B
  N27: EL817_1.Pin_1, R3.Pin_1
  N28: EL817_1.Pin_4, IN.pin2, EL817_2.Pin_4, OUT.pin2, Mod2.pin3#2, D1.cathode, D2.cathode
  N29: EL817_1.Pin_3, R4.Pin_0
  N30: TIP120_2.base, R4.Pin_1
  N31: TIP120_2.collector, IN.pin1, D1.anode
  N32: TIP120_2.emitter, TIP120_3.emitter, Mod2.pin3#3
  N33: EL817_2.Pin_1, R5.Pin_1
  N34: EL817_2.Pin_3, R6.Pin_0
  N35: TIP120_3.base, R6.Pin_1
  N36: TIP120_3.collector, OUT.pin1, D2.anode

notes:
  5+ (IN)
  5GND
  12GND
  12+
  5V
  12V
  + P_UP
  - P_DOWN
  TRIG_P_UP
  TRIG_P_DOWN
  TRIG_AUTO_START
  TRIG_STOP
  MAINS 220V

custom parts:
  generic-ac-power-supply: Generic ac power supply module. Use as is, or customize the svgs to fit your particular device (as they are all different.) Provides AC input and single DC output. PCB is generic and will need modifications if you intend to do a pcb mount.
  LCM1602 IIC: I2C-Module to use a 1602 or 2004 LCD on with the wire.h libory Serial LCD Modul
